// Logisim project Máquina de café-projeto.circ as structural Verilog: 4 circuits, main circuit Display
module Display (
  input  A,
  input  B,
  output a_2,
  output b_2,
  output c,
  output d,
  output e,
  output f,
  output g
);

  wire not_1_out, not_2_out, not_3_out, not_5_out, not_6_out;

  not not_1 (not_1_out, B);
  not not_2 (not_2_out, A);
  not not_3 (not_3_out, B);
  not not_4 (e, B);
  not not_5 (not_5_out, A);
  not not_6 (not_6_out, B);
  or or_1 (a_2, not_1_out, A);
  or or_2 (c, not_2_out, B);
  or or_3 (d, not_3_out, A);
  and and_1 (f, not_5_out, not_6_out);

  assign b_2 = 1'b1;
  assign g = A;
endmodule

module Moedeiro (
);

  wire and_1_out, and_2_out, and_3_out, and_4_out, and_5_out, and_6_out, and_7_out, clock_1_out, D1_q, D1_qn,
       D2_q, D2_qn, display_1_a_2, display_1_b_2, display_1_c, display_1_d, display_1_e, display_1_f,
       display_1_g, M1_out, M2_out, nand_1_out, not_1_out, or_1_out, or_2_out;

  Button M1 (.out(M1_out));
  Button M2 (.out(M2_out));
  Clock clock_1 (.out(clock_1_out));
  and and_1 (and_1_out, D2_q, D1_qn);
  and and_2 (and_2_out, M1_out, D2_qn, D1_q);
  not not_1 (not_1_out, M1_out);
  and and_3 (and_3_out, M1_out, D1_qn);
  and and_4 (and_4_out, M2_out, D2_q, D1_qn);
  or or_1 (or_1_out, and_1_out, and_2_out, and_5_out);
  and and_5 (and_5_out, not_1_out, M2_out, D2_qn);
  or or_2 (or_2_out, and_3_out, and_4_out, and_6_out);
  and and_6 (and_6_out, D1_q, not_1_out, D2_qn);
  D_Flip_Flop D2 (.clk(clock_1_out), .D(or_1_out), .Q(D2_q), .Qn(D2_qn), .en(nand_1_out));  // open: preset, reset
  D_Flip_Flop D1 (.clk(clock_1_out), .D(or_2_out), .Q(D1_q), .Qn(D1_qn), .en(nand_1_out));  // open: preset, reset
  and and_7 (and_7_out, D2_q, D1_q);
  Display display_1 (
    .A(D2_q), .B(D1_q), .a_2(display_1_a_2), .b_2(display_1_b_2), .c(display_1_c), .d(display_1_d),
    .e(display_1_e), .f(display_1_f), .g(display_1_g));
  LED L (.in(and_7_out));
  _7_Segment_Display u_7_segment_display_1 (
    .g(display_1_g), .f(display_1_f), .a(display_1_a_2), .b(display_1_b_2), .e(display_1_e), .d(display_1_d),
    .c(display_1_c));  // open: dp
  nand nand_1 (nand_1_out, display_1_b_2, display_1_c, display_1_d, display_1_g, display_1_a_2);
endmodule

module \módulo_para_servir_café  (
);

  wire and_1_out, and_2_out, and_3_out, and_4_out, and_5_out, and_6_out, B_out, clock_1_out, D0_q, D0_qn,
       D1_q, D1_qn, D2_q, D2_qn, or_1_out, or_2_out;

  Button B (.out(B_out));
  and and_1 (and_1_out, D2_q, D0_qn);
  Clock clock_1 (.out(clock_1_out));
  or or_1 (or_1_out, and_1_out, and_2_out);
  and and_2 (and_2_out, D1_q, D0_q);
  and and_3 (and_3_out, D1_q, D0_qn);
  or or_2 (or_2_out, and_3_out, and_4_out);
  and and_4 (and_4_out, D0_q, D2_qn, D1_qn);
  and and_5 (and_5_out, B_out, D0_qn);
  and and_6 (and_6_out, D0_q, D2_q);
  D_Flip_Flop D2 (.clk(clock_1_out), .D(or_1_out), .Q(D2_q), .Qn(D2_qn));  // open: preset, en, reset
  D_Flip_Flop D1 (.clk(clock_1_out), .D(or_2_out), .Q(D1_q), .Qn(D1_qn));  // open: preset, en, reset
  D_Flip_Flop D0 (.clk(clock_1_out), .D(and_5_out), .Q(D0_q), .Qn(D0_qn));  // open: preset, en, reset
  LED L (.in(and_6_out));
endmodule

module \Máquina_de_café  (
);

  wire and_1_out, and_2_out, and_3_out, and_4_out, and_5_out, and_6_out, and_7_out, and_8_out, and_9_out,
       and_10_out, and_11_out, and_12_out, and_13_out, and_14_out, B_out, clock_1_out, clock_2_out, D0_q,
       D0_qn, D1_2_q, D1_2_qn, D1_q, D1_qn, D2_2_q, D2_2_qn, D2_q, D2_qn, display_1_a_2, display_1_b_2,
       display_1_c, display_1_d, display_1_e, display_1_f, display_1_g, M1_out, M2_out, nand_1_out,
       not_1_out, or_1_out, or_2_out, or_3_out, or_4_out;

  Button M1 (.out(M1_out));
  Button M2 (.out(M2_out));
  Clock clock_1 (.out(clock_1_out));
  Button B (.out(B_out));
  and and_1 (and_1_out, D2_q, D1_qn);
  and and_2 (and_2_out, and_14_out, B_out);
  Clock clock_2 (.out(clock_2_out));
  and and_3 (and_3_out, M1_out, D2_qn, D1_q);
  not not_1 (not_1_out, M1_out);
  and and_4 (and_4_out, M1_out, D1_qn);
  and and_5 (and_5_out, M2_out, D2_q, D1_qn);
  and and_6 (and_6_out, D2_2_q, D0_qn);
  and and_7 (and_7_out, D1_2_q, D0_q);
  and and_8 (and_8_out, D1_2_q, D0_qn);
  or or_1 (or_1_out, and_1_out, and_3_out, and_9_out);
  and and_9 (and_9_out, not_1_out, M2_out, D2_qn);
  or or_2 (or_2_out, and_4_out, and_5_out, and_10_out);
  and and_10 (and_10_out, D1_q, not_1_out, D2_qn);
  or or_3 (or_3_out, and_6_out, and_7_out);
  and and_11 (and_11_out, D0_q, D2_2_qn, D1_2_qn);
  and and_12 (and_12_out, and_2_out, D0_qn);
  D_Flip_Flop D2 (
    .clk(clock_1_out), .D(or_1_out), .Q(D2_q), .Qn(D2_qn), .en(nand_1_out), .reset(and_13_out));  // open: preset
  D_Flip_Flop D1 (
    .clk(clock_1_out), .D(or_2_out), .Q(D1_q), .Qn(D1_qn), .en(nand_1_out), .reset(and_13_out));  // open: preset
  D_Flip_Flop D2_2 (.clk(clock_2_out), .D(or_3_out), .Q(D2_2_q), .Qn(D2_2_qn));  // open: preset, en, reset
  or or_4 (or_4_out, and_8_out, and_11_out);
  D_Flip_Flop D0 (.clk(clock_2_out), .D(and_12_out), .Q(D0_q), .Qn(D0_qn));  // open: preset, en, reset
  and and_13 (and_13_out, D0_q, D2_2_q);
  and and_14 (and_14_out, D2_q, D1_q);
  D_Flip_Flop D1_2 (.clk(clock_2_out), .D(or_4_out), .Q(D1_2_q), .Qn(D1_2_qn));  // open: preset, en, reset
  LED L (.in(and_13_out));
  Display display_1 (
    .A(D2_q), .B(D1_q), .a_2(display_1_a_2), .b_2(display_1_b_2), .c(display_1_c), .d(display_1_d),
    .e(display_1_e), .f(display_1_f), .g(display_1_g));
  LED L_2 (.in(and_14_out));
  _7_Segment_Display u_7_segment_display_1 (
    .g(display_1_g), .f(display_1_f), .a(display_1_a_2), .b(display_1_b_2), .e(display_1_e), .d(display_1_d),
    .c(display_1_c));  // open: dp
  nand nand_1 (nand_1_out, display_1_b_2, display_1_c, display_1_d, display_1_g, display_1_a_2);
endmodule
